// Digital circuit Ej6.dig as structural Verilog
module Ej6 (
  input  A0,
  input  A1,
  input  A2,
  input  A3,
  input  A4,
  input  A5,
  input  A6,
  input  A7,
  input  B0,
  input  B1,
  input  B2,
  input  B3,
  input  B4,
  input  B5,
  input  B6,
  input  B7,
  input  CI,
  input  VCC1,
  input  GND1,
  input  GND2,
  input  VCC2
);

  wire _7483_1_pin2, _7483_1_pin6, _7483_1_pin9, _7483_1_pin14, _7483_1_pin15, _7483_2_pin2, _7483_2_pin6,
       _7483_2_pin9, _7483_2_pin14, _7483_2_pin15;

  _7483 _7483_1 (
    .pin1(A3), .pin2(_7483_1_pin2), .pin3(A2), .pin4(B2), .pin5(VCC1), .pin6(_7483_1_pin6), .pin7(B1),
    .pin8(A1), .pin9(_7483_1_pin9), .pin10(A0), .pin11(B0), .pin12(GND1), .pin13(CI), .pin14(_7483_1_pin14),
    .pin15(_7483_1_pin15), .pin16(B3));
  _7483 _7483_2 (
    .pin1(A7), .pin2(_7483_2_pin2), .pin3(A6), .pin4(B6), .pin5(VCC2), .pin6(_7483_2_pin6), .pin7(B5),
    .pin8(A5), .pin9(_7483_2_pin9), .pin10(A4), .pin11(B4), .pin12(GND2), .pin13(_7483_1_pin14),
    .pin14(_7483_2_pin14), .pin15(_7483_2_pin15), .pin16(B7));
  LED S0 (.in(_7483_1_pin9));
  LED S1 (.in(_7483_1_pin6));
  LED S2 (.in(_7483_1_pin2));
  LED S3 (.in(_7483_1_pin15));
  LED S4 (.in(_7483_2_pin9));
  LED S5 (.in(_7483_2_pin6));
  LED S6 (.in(_7483_2_pin2));
  LED S7 (.in(_7483_2_pin15));
  LED CO (.in(_7483_2_pin14));

  // Notes on the sheet:
  //   VCC1: default 1
  //   VCC2: default 1
endmodule
