// Digital circuit Ej1C.dig as structural Verilog
module Ej1C (
  input  [1:0] A19___A20,
  input  [18:0] A0___A18,
  input  [15:0] D0___D15,
  input  Escritura,
  input  Lectura,
  input  [15:0] D16___D31
);

  wire decoder_1_out_0, decoder_1_out_1, decoder_1_out_2, decoder_1_out_3;

  Decoder #(.Selector_Bits(2)) decoder_1 (
    .sel(A19___A20), .out_0(decoder_1_out_0), .out_1(decoder_1_out_1), .out_2(decoder_1_out_2),
    .out_3(decoder_1_out_3));
  EEPROM #(.AddrBits(19), .Bits(16)) eeprom_1 (
    .A(A0___A18), .CS(decoder_1_out_3), .WE(Escritura), .OE(Lectura), .D(D0___D15));
  EEPROM #(.AddrBits(19), .Bits(16)) eeprom_2 (
    .A(A0___A18), .CS(decoder_1_out_3), .WE(Escritura), .OE(Lectura), .D(D16___D31));
  EEPROM #(.AddrBits(19), .Bits(16)) eeprom_3 (
    .A(A0___A18), .CS(decoder_1_out_2), .WE(Escritura), .OE(Lectura), .D(D0___D15));
  EEPROM #(.AddrBits(19), .Bits(16)) eeprom_4 (
    .A(A0___A18), .CS(decoder_1_out_2), .WE(Escritura), .OE(Lectura), .D(D16___D31));
  EEPROM #(.AddrBits(19), .Bits(16)) eeprom_5 (
    .A(A0___A18), .CS(decoder_1_out_1), .WE(Escritura), .OE(Lectura), .D(D0___D15));
  EEPROM #(.AddrBits(19), .Bits(16)) eeprom_6 (
    .A(A0___A18), .CS(decoder_1_out_1), .WE(Escritura), .OE(Lectura), .D(D16___D31));
  EEPROM #(.AddrBits(19), .Bits(16)) eeprom_7 (
    .A(A0___A18), .CS(decoder_1_out_0), .WE(Escritura), .OE(Lectura), .D(D0___D15));
  EEPROM #(.AddrBits(19), .Bits(16)) eeprom_8 (
    .A(A0___A18), .CS(decoder_1_out_0), .WE(Escritura), .OE(Lectura), .D(D16___D31));

  // Notes on the sheet:
  //   1572866
  //   2097154
  //   2M x 32 con CI de 512K x 16
  //   1048577
  //   1572865
  //   contents of eeprom_3 (hex, n*v repeats v):
  //   21*0,82
  //   contents of eeprom_4 (hex, n*v repeats v):
  //   21*0,82
  //   Direcciones
  //   524288
  //   1048576
  //   0
  //   524287
  //   contents of eeprom_7 (hex, n*v repeats v):
  //   0,1
  //   contents of eeprom_8 (hex, n*v repeats v):
  //   0,1
endmodule
