// Digital circuit Ej1.dig as structural Verilog
module Ej1 (
  input  A0,
  input  A1,
  input  A2,
  input  A3
);

  wire and_1_out, and_2_out, and_3_out, and_4_out, and_5_out, and_6_out, and_7_out, and_8_out, and_9_out,
       and_10_out, and_11_out, and_12_out, or_1_out, or_2_out;

  and and_1 (and_1_out, ~A0, ~A1);  // And
  and and_2 (and_2_out, ~A0, ~A1);  // And
  and and_3 (and_3_out, ~A0, A1);  // And
  and and_4 (and_4_out, ~A0, ~A1);  // And
  and and_5 (and_5_out, and_3_out, ~A2);  // And
  and and_6 (and_6_out, and_4_out, ~A2);  // And
  and and_7 (and_7_out, and_1_out, A2);
  and and_8 (and_8_out, and_2_out, ~A2);  // And
  and and_9 (and_9_out, and_7_out, ~A3);  // And
  and and_10 (and_10_out, and_8_out, A3);
  and and_11 (and_11_out, and_5_out, ~A3);  // And
  and and_12 (and_12_out, and_6_out, A3);
  or or_1 (or_1_out, and_11_out, and_12_out);
  or or_2 (or_2_out, and_9_out, and_10_out);
  LED S0 (.in(or_1_out));
  LED S1 (.in(or_2_out));
endmodule
