// Digital circuit Ej2.dig as structural Verilog
module Ej2 (
  input  A0,
  input  A1
);

  wire and_1_out, and_2_out, and_3_out, and_4_out;

  and and_1 (and_1_out, ~A0, ~A1);  // And
  and and_2 (and_2_out, A0, ~A1);  // And
  and and_3 (and_3_out, ~A0, A1);  // And
  and and_4 (and_4_out, A0, A1);
  LED S0 (.in(and_1_out));
  LED S1 (.in(and_2_out));
  LED S2 (.in(and_3_out));
  LED S3 (.in(and_4_out));
endmodule
