// Digital circuit Sumador.dig as structural Verilog
module Sumador (
  input  B0,
  input  C0,
  input  A0,
  input  B1,
  input  A1,
  input  B2,
  input  A2,
  output out_4
);

  wire add_1_c_o, add_1_s, add_2_c_o, add_2_s, add_3_s;

  Add add_1 (.a(A0), .b(B0), .c_i(C0), .s(add_1_s), .c_o(add_1_c_o));
  Add add_2 (.a(A1), .b(B1), .c_i(add_1_c_o), .s(add_2_s), .c_o(add_2_c_o));
  Add add_3 (.a(A2), .b(B2), .c_i(add_2_c_o), .s(add_3_s), .c_o(out_4));
  LED e0 (.in(add_1_s));
  LED e1 (.in(add_2_s));
  LED e2 (.in(add_3_s));
endmodule
