// Digital circuit Ej1A.dig as structural Verilog
module Ej1A (
  input  [1:0] A15___A16,
  input  [14:0] A0___A14,
  input  [7:0] D0___D7,
  input  Lectura,
  input  Escritura
);

  wire decoder_1_out_0, decoder_1_out_1, decoder_1_out_2, decoder_1_out_3;

  Decoder #(.Selector_Bits(2)) decoder_1 (
    .sel(A15___A16), .out_0(decoder_1_out_0), .out_1(decoder_1_out_1), .out_2(decoder_1_out_2),
    .out_3(decoder_1_out_3));
  EEPROM #(.AddrBits(15), .Bits(8)) eeprom_1 (
    .A(A0___A14), .CS(decoder_1_out_3), .WE(Escritura), .OE(Lectura), .D(D0___D7));
  EEPROM #(.AddrBits(15), .Bits(8)) eeprom_2 (
    .A(A0___A14), .CS(decoder_1_out_2), .WE(Escritura), .OE(Lectura), .D(D0___D7));
  EEPROM #(.AddrBits(15), .Bits(8)) eeprom_3 (
    .A(A0___A14), .CS(decoder_1_out_1), .WE(Escritura), .OE(Lectura), .D(D0___D7));
  EEPROM #(.AddrBits(15), .Bits(8)) eeprom_4 (
    .A(A0___A14), .CS(decoder_1_out_0), .WE(Escritura), .OE(Lectura), .D(D0___D7));

  // Notes on the sheet:
  //   128 K x 8 con CI de 32 K x 8
  //   98305
  //   131072
  //   contents of eeprom_2 (hex, n*v repeats v):
  //   21*0,82
  //   65536
  //   98304
  //   Direcciones
  //   32768
  //   65536
  //   0
  //   32767
endmodule
