// Digital circuit Ej1B.dig as structural Verilog
module Ej1B (
  input  [1:0] A19___A20,
  input  [18:0] A0___A18,
  input  [7:0] D0___D7,
  input  Lectura,
  input  Escritura
);

  wire decoder_1_out_0, decoder_1_out_1, decoder_1_out_2, decoder_1_out_3;

  Decoder #(.Selector_Bits(2)) decoder_1 (
    .sel(A19___A20), .out_0(decoder_1_out_0), .out_1(decoder_1_out_1), .out_2(decoder_1_out_2),
    .out_3(decoder_1_out_3));
  EEPROM #(.AddrBits(19), .Bits(8)) eeprom_1 (
    .A(A0___A18), .CS(decoder_1_out_3), .WE(Escritura), .OE(Lectura), .D(D0___D7));
  EEPROM #(.AddrBits(19), .Bits(8)) eeprom_2 (
    .A(A0___A18), .CS(decoder_1_out_2), .WE(Escritura), .OE(Lectura), .D(D0___D7));
  EEPROM #(.AddrBits(19), .Bits(8)) eeprom_3 (
    .A(A0___A18), .CS(decoder_1_out_1), .WE(Escritura), .OE(Lectura), .D(D0___D7));
  EEPROM #(.AddrBits(19), .Bits(8)) eeprom_4 (
    .A(A0___A18), .CS(decoder_1_out_0), .WE(Escritura), .OE(Lectura), .D(D0___D7));

  // Notes on the sheet:
  //   2M x 8 con CI de 512K x 8
  //   1572866
  //   2097154
  //   contents of eeprom_2 (hex, n*v repeats v):
  //   21*0,82
  //   1048577
  //   1572865
  //   Direcciones
  //   524288
  //   1048576
  //   0
  //   524287
endmodule
