// Digital circuit Ej1D.dig as structural Verilog
module Ej1D (
  input  [1:0] A32___A33,
  input  [31:0] A0___A31,
  input  [3:0] D0___D3,
  input  Escritura,
  input  Lectura,
  input  [3:0] D4___D7
);

  wire decoder_1_out_0, decoder_1_out_1, decoder_1_out_2, decoder_1_out_3;

  Decoder #(.Selector_Bits(2)) decoder_1 (
    .sel(A32___A33), .out_0(decoder_1_out_0), .out_1(decoder_1_out_1), .out_2(decoder_1_out_2),
    .out_3(decoder_1_out_3));
  EEPROM #(.AddrBits(24), .Bits(4)) eeprom_1 (
    .A(A0___A31[23:0]), .CS(decoder_1_out_3), .WE(Escritura), .OE(Lectura), .D(D0___D3));
  EEPROM #(.AddrBits(24), .Bits(4)) eeprom_2 (
    .A(A0___A31[23:0]), .CS(decoder_1_out_3), .WE(Escritura), .OE(Lectura), .D(D4___D7));
  EEPROM #(.AddrBits(24), .Bits(4)) eeprom_3 (
    .A(A0___A31[23:0]), .CS(decoder_1_out_2), .WE(Escritura), .OE(Lectura), .D(D0___D3));
  EEPROM #(.AddrBits(24), .Bits(4)) eeprom_4 (
    .A(A0___A31[23:0]), .CS(decoder_1_out_2), .WE(Escritura), .OE(Lectura), .D(D4___D7));
  EEPROM #(.AddrBits(24), .Bits(4)) eeprom_5 (
    .A(A0___A31[23:0]), .CS(decoder_1_out_1), .WE(Escritura), .OE(Lectura), .D(D0___D3));
  EEPROM #(.AddrBits(24), .Bits(4)) eeprom_6 (
    .A(A0___A31[23:0]), .CS(decoder_1_out_1), .WE(Escritura), .OE(Lectura), .D(D4___D7));
  EEPROM #(.AddrBits(24), .Bits(4)) eeprom_7 (
    .A(A0___A31[23:0]), .CS(decoder_1_out_0), .WE(Escritura), .OE(Lectura), .D(D0___D3));
  EEPROM #(.AddrBits(24), .Bits(4)) eeprom_8 (
    .A(A0___A31[23:0]), .CS(decoder_1_out_0), .WE(Escritura), .OE(Lectura), .D(D4___D7));
  // Pins of 24 and 32 bits meet at A0___A31

  // Notes on the sheet:
  //   16 G x 8 con CI de 4 G x 4
  //   12884901890
  //   17179869186
  //   8589934593
  //   12884901889
  //   contents of eeprom_3 (hex, n*v repeats v):
  //   21*0,82
  //   contents of eeprom_4 (hex, n*v repeats v):
  //   21*0,82
  //   Direcciones
  //   4294967296
  //   8589934592
  //   0
  //   4294967295
  //   contents of eeprom_7 (hex, n*v repeats v):
  //   0,1
  //   contents of eeprom_8 (hex, n*v repeats v):
  //   0,1
endmodule
